// Logisim project C208_AULAS29.circ as structural Verilog: 6 circuits, main circuit main
module main (
  input  CLEAR
);

  wire ALU_SRC, CLK, LOAD, MEM_TO_REG, REG_DEST, REG_W, registerfile_1_p7, STORE;
  wire [3:0] ALU_OP;
  wire [4:0] mipsprogramrom_1_p2_2, multiplexer_1_out;
  wire [5:0] FUNCT, OPCODE;
  wire [20:6] mipsprogramrom_1_p2;
  wire [31:0] adder_1_out, bit_extender_1_out, mips_alu_1_p4, mips_ram_1_p6, multiplexer_2_out, register_1_q,
       registerfile_1_p1, registerfile_1_p8;

  Clock u_CLK (.out(CLK));
  Adder #(.width(32)) adder_1 (.a(register_1_q), .b(32'h4), .out(adder_1_out));  // open: cin, cout
  UC uc_1 (
    .in_1(OPCODE[0]), .in_2(OPCODE[1]), .in_3(OPCODE[2]), .in_4(OPCODE[3]), .in_5(OPCODE[4]),
    .in_6(OPCODE[5]), .in_7(FUNCT[0]), .in_8(FUNCT[1]), .in_9(FUNCT[2]), .in_10(FUNCT[3]), .in_11(FUNCT[4]),
    .in_12(FUNCT[5]), .REG_DEST(REG_DEST), .REG_W(REG_W), .ALU_SRC(ALU_SRC), .LOAD(LOAD), .STORE(STORE),
    .MEM_TO_REG(MEM_TO_REG), .ALU_OP(ALU_OP));
  Register #(.width(32)) register_1 (.D(adder_1_out), .Q(register_1_q), .clk(CLK));  // open: en, clr
  // MIPSProgramROM mipsprogramrom_1: pin names not known; wires that end beside it: register_1_q, {OPCODE, mipsprogramrom_1_p2_2, mipsprogramrom_1_p2, FUNCT}
  Multiplexer #(.width(5)) multiplexer_1 (
    .in0(mipsprogramrom_1_p2[15:11]), .in1(mipsprogramrom_1_p2[20:16]), .out(multiplexer_1_out),
    .sel(REG_DEST));  // open: en
  assign bit_extender_1_out = {{16{1'b0}}, {mipsprogramrom_1_p2[15:6], FUNCT}};  // Bit_Extender bit_extender_1
  // RegisterFile registerfile_1: pin names not known; wires that end beside it: registerfile_1_p1, CLK, REG_W, multiplexer_1_out, mipsprogramrom_1_p2_2, mipsprogramrom_1_p2[20:16], registerfile_1_p7, registerfile_1_p8
  Multiplexer #(.width(32)) multiplexer_2 (
    .in0(registerfile_1_p8), .in1(bit_extender_1_out), .out(multiplexer_2_out), .sel(ALU_SRC));  // open: en
  // Mips_ALU mips_alu_1: pin names not known; wires that end beside it: registerfile_1_p7, multiplexer_2_out, ALU_OP, mips_alu_1_p4, registerfile_1_p8
  // MIPS_RAM mips_ram_1: pin names not known; wires that end beside it: mips_alu_1_p4[19:0], STORE, CLK, LOAD, CLEAR, mips_ram_1_p6
  Multiplexer #(.width(32)) multiplexer_3 (
    .in0(mips_alu_1_p4), .in1(mips_ram_1_p6), .out(registerfile_1_p1), .sel(MEM_TO_REG));  // open: en

  // Notes on the sheet:
  //   SA
  //   IMEDIATO
  //   DEST_R
  //   DEST_I
  //   R
  //   I
endmodule

module aula1 (
  input  [31:0] in_1,
  input  [31:0] DADO_A_SER_ESCRITO,
  input  \HABILITA_GRAVAÇÃO ,
  output [5:0] FUNCT,
  output [4:0] SHIFT_AMOUNT,
  output [31:0] DADO_LIDO__ORIGEM_1,
  output [4:0] DESTINO,
  output [4:0] ORIGEM_2,
  output [4:0] ORIGEM_1,
  output [5:0] OPCODE,
  output [31:0] DADO_LIDO__ORIGEM_2
);

  wire CLOCK_out;

  // MIPSProgramROM mipsprogramrom_1: pin names not known; wires that end beside it: in_1, {OPCODE, ORIGEM_1, ORIGEM_2, DESTINO, SHIFT_AMOUNT, FUNCT}
  Clock CLOCK (.out(CLOCK_out));
  // RegisterFile registerfile_1: pin names not known; wires that end beside it: DADO_A_SER_ESCRITO, CLOCK_out, \HABILITA_GRAVAÇÃO , DESTINO, ORIGEM_1, ORIGEM_2, DADO_LIDO__ORIGEM_1, DADO_LIDO__ORIGEM_2

  // Notes on the sheet:
  //   ENDEREÇO
  //   DADO
  //   CONTROLE
  //   DADO
  //   DADO
endmodule

module Tipo_R (
  input  [3:0] ALU_OP,
  input  REG_W,
  output [5:0] FUNCT,
  output [4:0] SHIFT_AMOUNT,
  output [4:0] DESTINO,
  output [4:0] ORIGEM_2,
  output [4:0] ORIGEM_1,
  output [5:0] OPCODE
);

  wire CLK_out, clock_1_out, registerfile_1_p1, registerfile_1_p7, registerfile_1_p8;
  wire [31:0] adder_1_out, register_1_q;

  Adder #(.width(32)) adder_1 (.a(register_1_q), .b(32'h4), .out(adder_1_out));  // open: cin, cout
  Register #(.width(32)) register_1 (.D(adder_1_out), .Q(register_1_q), .clk(clock_1_out));  // open: en, clr
  Clock clock_1 (.out(clock_1_out));
  // MIPSProgramROM mipsprogramrom_1: pin names not known; wires that end beside it: register_1_q, {OPCODE, ORIGEM_1, ORIGEM_2, DESTINO, SHIFT_AMOUNT, FUNCT}
  Clock CLK (.out(CLK_out));
  // RegisterFile registerfile_1: pin names not known; wires that end beside it: registerfile_1_p1, CLK_out, REG_W, DESTINO, ORIGEM_1, ORIGEM_2, registerfile_1_p7, registerfile_1_p8
  // Mips_ALU mips_alu_1: pin names not known; wires that end beside it: registerfile_1_p7, registerfile_1_p8, ALU_OP, registerfile_1_p1

  // Notes on the sheet:
  //   ENDEREÇO
  //   CONTROLE
endmodule

module TIPO_R___I (
  input  REG_DEST,
  input  I,
  input  [3:0] ALU_OP,
  input  REG_W
);

  wire CLK_out, clock_1_out, registerfile_1_p1, registerfile_1_p7;
  wire [4:0] multiplexer_1_out;
  wire [31:0] adder_1_out, bit_extender_1_out, mipsprogramrom_1_p2, multiplexer_2_out, register_1_q,
       registerfile_1_p8;

  Adder #(.width(32)) adder_1 (.a(register_1_q), .b(32'h4), .out(adder_1_out));  // open: cin, cout
  Register #(.width(32)) register_1 (.D(adder_1_out), .Q(register_1_q), .clk(clock_1_out));  // open: en, clr
  Clock clock_1 (.out(clock_1_out));
  // MIPSProgramROM mipsprogramrom_1: pin names not known; wires that end beside it: register_1_q, mipsprogramrom_1_p2
  Multiplexer #(.width(5)) multiplexer_1 (
    .in0(mipsprogramrom_1_p2[15:11]), .in1(mipsprogramrom_1_p2[20:16]), .out(multiplexer_1_out),
    .sel(REG_DEST));  // open: en
  Clock CLK (.out(CLK_out));
  assign bit_extender_1_out = {{16{1'b0}}, mipsprogramrom_1_p2[15:0]};  // Bit_Extender bit_extender_1
  // RegisterFile registerfile_1: pin names not known; wires that end beside it: registerfile_1_p1, CLK_out, REG_W, multiplexer_1_out, mipsprogramrom_1_p2[25:21], mipsprogramrom_1_p2[20:16], registerfile_1_p7, registerfile_1_p8
  Multiplexer #(.width(32)) multiplexer_2 (
    .in0(registerfile_1_p8), .in1(bit_extender_1_out), .out(multiplexer_2_out), .sel(I));  // open: en
  // Mips_ALU mips_alu_1: pin names not known; wires that end beside it: registerfile_1_p7, multiplexer_2_out, ALU_OP, registerfile_1_p1

  // Notes on the sheet:
  //   FUNCT
  //   SA
  //   IMEDIATO
  //   DEST_R
  //   DEST_I
  //   CONTROLE
  //   R
  //   ALU_SRC
endmodule

module TIPO_LOAD___STORE (
  input  REG_DEST,
  input  MEM_TO_REG,
  input  STORE,
  input  LOAD,
  input  I,
  input  [3:0] ALU_OP,
  input  CLEAR,
  input  REG_W
);

  wire CLK, registerfile_1_p7;
  wire [4:0] multiplexer_1_out;
  wire [31:0] adder_1_out, bit_extender_1_out, mips_alu_1_p4, mips_ram_1_p6, mipsprogramrom_1_p2,
       multiplexer_2_out, register_1_q, registerfile_1_p1, registerfile_1_p8;

  Adder #(.width(32)) adder_1 (.a(register_1_q), .b(32'h4), .out(adder_1_out));  // open: cin, cout
  Register #(.width(32)) register_1 (.D(adder_1_out), .Q(register_1_q), .clk(CLK));  // open: en, clr
  // MIPSProgramROM mipsprogramrom_1: pin names not known; wires that end beside it: register_1_q, mipsprogramrom_1_p2
  Multiplexer #(.width(5)) multiplexer_1 (
    .in0(mipsprogramrom_1_p2[15:11]), .in1(mipsprogramrom_1_p2[20:16]), .out(multiplexer_1_out),
    .sel(REG_DEST));  // open: en
  Clock u_CLK (.out(CLK));
  assign bit_extender_1_out = {{16{1'b0}}, mipsprogramrom_1_p2[15:0]};  // Bit_Extender bit_extender_1
  // RegisterFile registerfile_1: pin names not known; wires that end beside it: registerfile_1_p1, CLK, REG_W, multiplexer_1_out, mipsprogramrom_1_p2[25:21], mipsprogramrom_1_p2[20:16], registerfile_1_p7, registerfile_1_p8
  Multiplexer #(.width(32)) multiplexer_2 (
    .in0(registerfile_1_p8), .in1(bit_extender_1_out), .out(multiplexer_2_out), .sel(I));  // open: en
  // Mips_ALU mips_alu_1: pin names not known; wires that end beside it: registerfile_1_p7, multiplexer_2_out, ALU_OP, mips_alu_1_p4, registerfile_1_p8
  Multiplexer #(.width(32)) multiplexer_3 (
    .in0(mips_alu_1_p4), .in1(mips_ram_1_p6), .out(registerfile_1_p1), .sel(MEM_TO_REG));  // open: en
  // MIPS_RAM mips_ram_1: pin names not known; wires that end beside it: mips_alu_1_p4[19:0], STORE, CLK, LOAD, CLEAR, mips_ram_1_p6

  // Notes on the sheet:
  //   FUNCT
  //   SA
  //   IMEDIATO
  //   DEST_R
  //   DEST_I
  //   CONTROLE
  //   R
  //   ALU_SRC
endmodule

// CONTROLE
module UC (
  input  in_1,
  input  in_2,
  input  in_3,
  input  in_4,
  input  in_5,
  input  in_6,
  input  in_7,
  input  in_8,
  input  in_9,
  input  in_10,
  input  in_11,
  input  in_12,
  output REG_DEST,
  output REG_W,
  output ALU_SRC,
  output LOAD,
  output STORE,
  output MEM_TO_REG,
  output [3:0] ALU_OP
);

  wire ADDIU, ADDU_out, and_1_out, and_2_out;

  and u_ADDIU (ADDIU, in_1, ~in_2, ~in_3, in_4, ~in_5, ~in_6);  // AND_Gate
  and SW (STORE, in_1, in_2, ~in_3, in_4, ~in_5, in_6);  // AND_Gate
  and LW (LOAD, in_1, in_2, ~in_3, ~in_4, ~in_5, in_6);  // AND_Gate
  and and_1 (and_1_out, ~in_1, ~in_2, ~in_3, ~in_4, ~in_5, ~in_6);  // AND_Gate
  and and_2 (and_2_out, in_7, ~in_8, ~in_9, ~in_10, ~in_11, in_12);  // AND_Gate
  and ADDU (ADDU_out, and_1_out, and_2_out);
  or or_1 (ALU_SRC, ADDIU, STORE, LOAD);
  or or_2 (REG_W, ADDIU, LOAD, ADDU_out);

  assign ALU_OP = 4'b0010;
  assign MEM_TO_REG = LOAD;
  assign REG_DEST = ALU_SRC;

  // Other names for the same wires on the sheet: B1 = in_1; B2 = in_2; B3 = in_3; B4 = in_4; B5 = in_5; B6 = in_6;
  //   F1 = in_7; F2 = in_8; F3 = in_9; F4 = in_10; F5 = in_11; F6 = in_12; LW = LOAD; SW = STORE

  // Notes on the sheet:
  //   UPCODE
  //   FUNCT
  //   CONTROLES
endmodule
