// Logisim project ULA.circ as structural Verilog: 1 circuit, main circuit ULA
module ULA (
  input  [7:0] A,
  input  [7:0] B,
  input  [2:0] Qtd_Bits_Deslocar,
  input  CIN,
  input  [3:0] OP,
  output [7:0] OP_2,
  output Add_COUT,
  output Sub_COUT
);

  wire [7:0] adder_1_out, and_1_out, multiplier_1_out, nand_1_out, nor_1_out, not_1_out, or_1_out,
       shifter_1_out, shifter_2_out, subtractor_1_out, undriven, xnor_1_out, xor_1_out;

  assign xnor_1_out = ~(A ^ B);  // XNOR_Gate xnor_1, 8 bits wide
  assign or_1_out = A | B;  // OR_Gate or_1, 8 bits wide
  Shifter #(.shift("lr")) shifter_1 (.in(A), .\dist (Qtd_Bits_Deslocar), .out(shifter_1_out));
  assign xor_1_out = A ^ B;  // XOR_Gate xor_1, 8 bits wide
  Multiplier multiplier_1 (.a(A), .b(B), .out(multiplier_1_out), .cin(undriven));  // open: cout
  assign nor_1_out = ~(A | B);  // NOR_Gate nor_1, 8 bits wide
  assign and_1_out = A & B;  // AND_Gate and_1, 8 bits wide
  Subtractor subtractor_1 (.a(A), .b(B), .out(subtractor_1_out), .bin(CIN), .bout(Sub_COUT));
  Shifter shifter_2 (.in(A), .\dist (Qtd_Bits_Deslocar), .out(shifter_2_out));
  assign nand_1_out = ~(A & B);  // NAND_Gate nand_1, 8 bits wide
  assign not_1_out = ~A;  // NOT_Gate not_1, 8 bits wide
  Adder adder_1 (.a(A), .b(B), .out(adder_1_out), .cin(CIN), .cout(Add_COUT));
  Multiplexer #(.select(4), .width(8), .enable("false")) multiplexer_1 (
    .in1(xnor_1_out), .in2(or_1_out), .in3(shifter_1_out), .in4(xor_1_out), .in5(multiplier_1_out),
    .in6(nor_1_out), .in7(and_1_out), .in9(subtractor_1_out), .in10(shifter_2_out), .in11(nand_1_out),
    .in12(not_1_out), .in15(adder_1_out), .out(OP_2), .sel(OP));  // open: in0, in8, in13, in14
endmodule
