// Logisim project circuito_base.circ as structural Verilog: 2 circuits, main circuit main
module main (
);

  wire BRANCH, CLK, IE, JMP, JR, JUMPSET, LINK, MLE, MSE, WE;
  wire [3:0] ALUOP;
  wire [4:0] multiplexer_3_out, multiplexer_5_out;
  wire [31:0] A, adder_2_out, B, C, imm, jaddr, jimm, mips_ram_1_p7, multiplexer_1_out, multiplexer_2_out,
       multiplexer_4_out, multiplexer_6_out, NEXTPC, offset, Op, PC, shifter_1_out, shifter_2_out, W;

  // Probe on PC
  Clock u_CLK (.out(CLK));
  Adder #(.width(32)) adder_1 (.a(PC), .b(32'h4), .out(NEXTPC));  // open: cin, cout
  Multiplexer #(.width(32)) multiplexer_1 (
    .in0({32{1'b0}}), .in1(offset), .out(multiplexer_1_out), .sel(BRANCH));  // open: en
  // Probe on multiplexer_1_out
  // Probe on jaddr
  // Probe on A
  Multiplexer #(.width(32)) multiplexer_2 (.in0(W), .in1(NEXTPC), .out(multiplexer_2_out), .sel(LINK));  // open: en
  Shifter #(.width(32), .shift("lr")) shifter_1 (.in(C), .\dist (5'b00010), .out(shifter_1_out));
  Adder #(.width(32)) adder_2 (.a(NEXTPC), .b(multiplexer_1_out), .out(adder_2_out));  // open: cin, cout
  Multiplexer #(.width(5)) multiplexer_3 (
    .in0(Op[15:11]), .in1(Op[20:16]), .out(multiplexer_3_out), .sel(IE));  // open: en
  Multiplexer #(.width(32)) multiplexer_4 (
    .in0(adder_2_out), .in1(jaddr), .out(multiplexer_4_out), .sel(JUMPSET));  // open: en
  // Probe on B
  Multiplexer #(.width(5)) multiplexer_5 (
    .in0(multiplexer_3_out), .in1({5{1'b1}}), .out(multiplexer_5_out), .sel(LINK));  // open: en
  Register #(.width(32)) register_1 (.D(multiplexer_4_out), .Q(PC), .clk(CLK));  // open: en, clr
  // RegisterFile registerfile_1: pin names not known; wires that end beside it: multiplexer_2_out, CLK, WE, multiplexer_5_out, Op[25:21], Op[20:16], A, B
  // MIPS_RAM mips_ram_1: pin names not known; wires that end beside it: shifter_1_out[19:0], B, MSE, CLK, MLE, 1'b0, mips_ram_1_p7
  // MIPSProgramROM mipsprogramrom_1: pin names not known; wires that end beside it: PC, Op
  // Probe on C
  Multiplexer #(.width(32)) multiplexer_6 (.in0(B), .in1(imm), .out(multiplexer_6_out), .sel(IE));  // open: en
  Multiplexer #(.width(32)) multiplexer_7 (.in0(C), .in1(mips_ram_1_p7), .out(W), .sel(MLE));  // open: en
  // Mips_ALU mips_alu_1: pin names not known; wires that end beside it: A, multiplexer_6_out, ALUOP, Op[10:6], C
  ctrl ctrl_1 (
    .Opcode(Op[31:26]), .Special(Op[5:0]), .out_3(IE), .out_4(WE), .out_5(MLE), .out_6(MSE), .out_7(JMP),
    .out_8(JUMPSET), .out_9(LINK), .out_10(JR), .out_11(ALUOP));
  assign imm = {{16{Op[15]}}, Op[15:0]};  // Bit_Extender bit_extender_1
  assign jimm = {{6{Op[25]}}, Op[25:0]};  // Bit_Extender bit_extender_2
  Shifter #(.width(32)) shifter_2 (.in(jimm), .\dist (5'b00010), .out(shifter_2_out));
  // Probe on ALUOP
  // Probe on imm
  // Probe on jimm
  Shifter #(.width(32)) shifter_3 (.in(imm), .\dist (5'b00010), .out(offset));
  Multiplexer #(.width(32)) multiplexer_8 (.in0(shifter_2_out), .in1(A), .out(jaddr), .sel(JR));  // open: en
  and and_1 (BRANCH, C[0], JMP);
  // Probe on Op[5:0]
  // Probe on Op[10:6]
  // Probe on Op[15:11]
  // Probe on Op[20:16]
  // Probe on Op[25:21]
  // Probe on Op[31:26]

  // Other names for the same wires on the sheet: special[5:0] = Op[5:0]; shamt[4:0] = Op[10:6]; rd[4:0] = Op[15:11];
  //   rt[4:0] = Op[20:16]; rs[4:0] = Op[25:21]; opcode[5:0] = Op[31:26]
endmodule

module ctrl (
  input  [5:0] Opcode,
  input  [5:0] Special,
  output out_3,
  output out_4,
  output out_5,
  output out_6,
  output out_7,
  output out_8,
  output out_9,
  output out_10,
  output [3:0] out_11
);

  wire ADDIU, ADDU, and_11_out, and_12_out, and_13_out, and_14_out, BEQ, BGTZ, BLEZ, J, ORI, SLL, SPECIAL_t,
       SUBU;
  wire [2:0] or_5_out;

  or or_1 (out_3, ADDIU, out_5, out_6);
  or or_2 (out_4, ADDIU, out_5, out_9, ADDU, ORI, SUBU, SLL);
  and and_1 (ADDIU, ~Opcode[5], ~Opcode[4], Opcode[3], ~Opcode[2], ~Opcode[1], Opcode[0]);  // AND_Gate
  and and_2 (BEQ, ~Opcode[5], ~Opcode[4], ~Opcode[3], Opcode[2], ~Opcode[1], ~Opcode[0]);  // AND_Gate
  and and_3 (BGTZ, ~Opcode[5], ~Opcode[4], ~Opcode[3], Opcode[2], Opcode[1], Opcode[0]);  // AND_Gate
  and and_4 (BLEZ, ~Opcode[5], ~Opcode[4], ~Opcode[3], Opcode[2], Opcode[1], ~Opcode[0]);  // AND_Gate
  and and_5 (J, ~Opcode[5], ~Opcode[4], ~Opcode[3], ~Opcode[2], Opcode[1], ~Opcode[0]);  // AND_Gate
  and and_6 (out_9, ~Opcode[5], ~Opcode[4], ~Opcode[3], ~Opcode[2], Opcode[1], Opcode[0]);  // AND_Gate
  and and_7 (out_5, Opcode[5], ~Opcode[4], ~Opcode[3], ~Opcode[2], Opcode[1], Opcode[0]);  // AND_Gate
  and and_8 (out_6, Opcode[5], ~Opcode[4], Opcode[3], ~Opcode[2], Opcode[1], Opcode[0]);  // AND_Gate
  and and_9 (SPECIAL_t, ~Opcode[5], ~Opcode[4], ~Opcode[3], ~Opcode[2], ~Opcode[1], ~Opcode[0]);  // AND_Gate
  and and_10 (ORI, ~Opcode[5], ~Opcode[4], Opcode[3], Opcode[2], ~Opcode[1], Opcode[0]);  // AND_Gate
  or or_3 (out_7, BEQ, BGTZ, BLEZ);
  or or_4 (out_8, out_10, out_9, J);
  and and_11 (and_11_out, Special[5], ~Special[4], ~Special[3], ~Special[2], ~Special[1], Special[0]);  // AND_Gate
  and and_12 (and_12_out, ~Special[5], ~Special[4], Special[3], ~Special[2], ~Special[1], ~Special[0]);  // AND_Gate
  and and_13 (and_13_out, Special[5], ~Special[4], ~Special[3], ~Special[2], Special[1], Special[0]);  // AND_Gate
  and and_14 (and_14_out, ~Special[5], ~Special[4], ~Special[3], ~Special[2], ~Special[1], ~Special[0]);  // AND_Gate
  and and_15 (ADDU, SPECIAL_t, and_11_out);
  and and_16 (out_10, SPECIAL_t, and_12_out);
  and and_17 (SUBU, SPECIAL_t, and_13_out);
  and and_18 (SLL, SPECIAL_t, and_14_out);
  or or_5 (or_5_out[0], ADDIU, ADDU, SUBU, out_5, out_6, BGTZ);
  or or_6 (or_5_out[1], SUBU, BEQ);
  or or_7 (or_5_out[2], SLL, BGTZ);
  Multiplexer #(.select(4), .width(4)) multiplexer_1 (
    .in1(4'b0010), .in2(4'b1001), .in3(4'b0110), .in4(4'b0000), .in5(4'b1101), .in8(4'b1111), .out(out_11),
    .sel({BLEZ, or_5_out}));  // open: in0, in6, in7, in9, in10, in11, in12, in13, in14, in15, en

  // Other names for the same wires on the sheet: ALUOP[3:0] = out_11; IE = out_3; JMP = out_7; JMPSET = out_8;
  //   JR = out_10; JAL = out_9; LINK = out_9; LW = out_5; MLE = out_5; MSE = out_6; SW = out_6; WE = out_4

  // Notes on the sheet:
  //   Add Imediate Unsigned Word
  //   Branch on Equal
  //   Branch on Greater Than Zero
  //   Branch on Less Than or Equal to Zero
  //   Jump
  //   Jump and Link
  //   Load Word
  //   Store Word
  //   OR Imm
  //   Add Unsigned Word
  //   Jump Register
  //   Substract Unsigned Word
  //   Shift Word Left Logical
endmodule
